# Fritzing sketch ato-schematic (saved by Fritzing 0.9.3b)
circuit board: 5.42573cm x 5.59507cm
breadboards: 1

parts:
  U1 = NodeMCU V1.0
  R1 = Resistor [tolerance=±5% resistance=220 package=THT]
  R2 = Resistor [tolerance=±5% resistance=220 package=THT]
  U2 = Sharp PC817 [package=THT]
  Q1 = NPN-Transistor [package="TO92 [THT]"]
  Water_Sensor = Screw terminal - 2 pins [package=THT]
  Water_Relay = Screw terminal - 2 pins [package=THT]
  12V_In = Screw terminal - 2 pins [package=THT]

nets:
  N1: U1.D1, R2.Pin_0
  N2: U1.3V3, Water_Sensor.pin2
  N3: U1.GND, U2.Pin_2, Q1.E, 12V_In.pin2
  N4: U1.Vin, U2.Pin_4, Water_Relay.pin1, 12V_In.pin1
  N5: U1.A0, Water_Sensor.pin1
  N6: R1.Pin_0, U2.Pin_3
  N7: R1.Pin_1, Q1.B
  N8: R2.Pin_1, U2.Pin_1
  N9: Q1.C, Water_Relay.pin2

custom parts:
  NodeMCU V1.0: ESP8266 based NodeMCU
